// Digital circuit 16-BIT INVERT.dig as structural Verilog
module _16_BIT_INVERT (
  input  [15:0] IN,
  input  INVERT,
  output [15:0] OUT
);

  _8_BIT_INVERT _8_bit_invert_1 (.IN(IN[7:0]), .INVERT(INVERT), .OUT(OUT[7:0]));
  _8_BIT_INVERT _8_bit_invert_2 (.IN(IN[15:8]), .INVERT(INVERT), .OUT(OUT[15:8]));
endmodule
