// Digital circuit 32-BIT INVERT.dig as structural Verilog
module _32_BIT_INVERT (
  input  [31:0] IN,
  input  INVERT,
  output [31:0] OUT
);

  _16_BIT_INVERT _16_bit_invert_1 (.IN(IN[15:0]), .INVERT(INVERT), .OUT(OUT[15:0]));
  _16_BIT_INVERT _16_bit_invert_2 (.IN(IN[31:16]), .INVERT(INVERT), .OUT(OUT[31:16]));
endmodule
