// Digital circuit 4-BIT INVERT.dig as structural Verilog
module _4_BIT_INVERT (
  input  [3:0] IN,
  input  INVERT,
  output [3:0] OUT
);

  xor xor_1 (OUT[0], IN[0], INVERT);
  xor xor_2 (OUT[1], IN[1], INVERT);
  xor xor_3 (OUT[2], IN[2], INVERT);
  xor xor_4 (OUT[3], IN[3], INVERT);
endmodule
