// Digital circuit 64-BIT INVERT.dig as structural Verilog
module _64_BIT_INVERT (
  input  [63:0] IN,
  input  INVERT,
  output [63:0] OUT
);

  _32_BIT_INVERT _32_bit_invert_1 (.IN(IN[31:0]), .INVERT(INVERT), .OUT(OUT[31:0]));
  _32_BIT_INVERT _32_bit_invert_2 (.IN(IN[63:32]), .INVERT(INVERT), .OUT(OUT[63:32]));
endmodule
