// Digital circuit 8-BIT INVERT.dig as structural Verilog
module _8_BIT_INVERT (
  input  [7:0] IN,
  input  INVERT,
  output [7:0] OUT
);

  _4_BIT_INVERT _4_bit_invert_1 (.IN(IN[3:0]), .INVERT(INVERT), .OUT(OUT[3:0]));
  _4_BIT_INVERT _4_bit_invert_2 (.IN(IN[7:4]), .INVERT(INVERT), .OUT(OUT[7:4]));
  // Pins of 1 and 8 bits meet at OUT
endmodule
