// Digital circuit CPU.dig as structural Verilog
module CPU (
  input  CLK,
  input  RESET,
  input  [63:0] X_IN,
  input  [63:0] M_IN,
  output [15:0] M_ADDR,
  output [63:0] M_OUT,
  output [63:0] M_WR
);

  wire and_1_out, not_1_out, not_2_out, or_1_out;
  wire [63:0] pulldown_1_out;

  PullDown #(.Bits(64)) pulldown_1 (.out(pulldown_1_out));
  // Not not_1 has open pins: in=open, out=not_1_out
  or or_1 (or_1_out, not_1_out, RESET);
  and and_1 (and_1_out, CLK, or_1_out);
  not not_2 (not_2_out, and_1_out);
  CounterPreset #(.Bits(8)) PC (.C(not_2_out));  // open: en, dir, in, ld, clr, out, ovf

  // Notes on the sheet:
  //   CLK: Hz: 100000
endmodule
